# Fritzing sketch schematic (saved by Fritzing 0.9.3b)
breadboards: 1

parts:
  Raspberry_Pi_1 = Raspberry Pi 3 [part_number=RPI-3-V1.2]
  Composant1 = Arduino Uno (Rev3)
  KY-1 = Keyes Relay [package=THT]
  KY-2 = Keyes Relay [package=THT]
  KY-3 = Keyes Relay [package=THT]
  KY-4 = Keyes Relay [package=THT]
  IR1 = TSOP312.., 314.. [package=THT]

nets:
  N1: Raspberry_Pi_1.GPIO2, Composant1.A4/SDA
  N2: Raspberry_Pi_1.GPIO3, Composant1.A5/SCL
  GND: Raspberry_Pi_1.GND, Composant1.GND, KY-1.ground, KY-2.ground, KY-3.ground, KY-4.ground, IR1.GND, IR1.Vs
  5V: Raspberry_Pi_1.5V, Composant1.5V, KY-1.power, KY-2.power, KY-3.power, KY-4.power
  N3: Composant1.D8, KY-1.signal
  N4: Composant1.D9_PWM, KY-2.signal
  N5: Composant1.D10_PWM/SS, KY-3.signal
  N6: Composant1.D11_PWM/MOSI, KY-4.signal
  N7: Composant1.D12/MISO, IR1.Data

custom parts:
  Keyes Relay: The Keyes 5V relay module is suitable for SCM development, home appliance control. It uses a 5V~12V TIL control signal which can control DC / AC signal.
